# Fritzing sketch hx-stomp-midi-switcher-breadboard (saved by Fritzing 0.9.3b)
breadboards: 1

parts:
  Part1 = Arduino Nano (Rev3.0)
  U1 = MIDI_CONN_FEMALE [package=din_5_female]
  OLED1 = OLED 128x64 I2C Monochrome Display
  S1 = Pushbutton [package="[THT]"]
  S2 = Pushbutton [package="[THT]"]
  S3 = Pushbutton [package="[THT]"]
  S4 = Pushbutton [package="[THT]"]
  S5 = Pushbutton [package="[THT]"]
  S6 = Pushbutton [package="[THT]"]
  S7 = Pushbutton [package="[THT]"]
  S8 = Pushbutton [package="[THT]"]
  R1 = Resistor [tolerance=±5% resistance=220 package=THT]
  Power_plug1 = Power plug

nets:
  N1: Part1.D1/TX, U1.MIDI_IN
  GND: Part1.GND, U1.NC1, OLED1.GND, S1.Pin_1, S1.Pin_2, S2.Pin_1, S2.Pin_2, S3.Pin_1, S3.Pin_2, S4.Pin_1, S4.Pin_2, S5.Pin_1, S5.Pin_2, S6.Pin_1, S6.Pin_2, S7.Pin_1, S7.Pin_2, S8.Pin_1, S8.Pin_2, Power_plug1.GND
  N2: Part1.D2, S1.Pin_3, S1.Pin_4
  N3: Part1.D3, S2.Pin_3, S2.Pin_4
  N4: Part1.D4, S3.Pin_3, S3.Pin_4
  N5: Part1.D5, S4.Pin_3, S4.Pin_4
  N6: Part1.D6, S5.Pin_3, S5.Pin_4
  N7: Part1.D7, S6.Pin_3, S6.Pin_4
  N8: Part1.D8, S7.Pin_3, S7.Pin_4
  N9: Part1.D9, S8.Pin_3, S8.Pin_4
  VIN: Part1.VIN, Power_plug1.VCC
  5V: Part1.5V, OLED1.VDD, R1.Pin_0
  N10: Part1.A5, OLED1.SCK
  N11: Part1.A4, OLED1.SDA
  N12: U1.MIDI_OUT, R1.Pin_1
