# Fritzing sketch hx-stomp-midi-switcher-stripboard (saved by Fritzing 0.9.3b)
stripboards: 1

parts:
  Part1 = Arduino Nano (Rev3.0)
  S1 = Pushbutton [package="[THT]"]
  S2 = Pushbutton [package="[THT]"]
  S3 = Pushbutton [package="[THT]"]
  S4 = Pushbutton [package="[THT]"]
  S5 = Pushbutton [package="[THT]"]
  S6 = Pushbutton [package="[THT]"]
  S7 = Pushbutton [package="[THT]"]
  S8 = Pushbutton [package="[THT]"]
  J1 = female pin header, 3 pins [form="♀ (female)"]
  J2 = female pin header, 4 pins [form="♀ (female)"]
  OLED1 = OLED 128x64 I2C Monochrome Display
  U1 = MIDI_CONN_FEMALE [package=din_5_female]
  R1 = Resistor [tolerance=±5% resistance=220 package=THT]

nets:
  N1: Part1.GND, S1.Pin_1, S2.Pin_1, S2.Pin_2, S3.Pin_1, S3.Pin_2, S4.Pin_1, S4.Pin_2, S5.Pin_1, S5.Pin_2, S6.Pin_1, S7.Pin_1, S7.Pin_2, S8.Pin_1, S8.Pin_2
  N2: Part1.D2, S8.Pin_4
  N3: Part1.D3, S7.Pin_4
  N4: Part1.D4, S6.Pin_3, S6.Pin_4, J2.pin2, OLED1.VDD
  N5: Part1.D5, S5.Pin_3, S5.Pin_4
  N6: Part1.D6, S4.Pin_3, S4.Pin_4
  N7: Part1.D7, S3.Pin_4
  N8: Part1.D8, S2.Pin_4
  N9: Part1.D9, S1.Pin_4
  N10: Part1.D12/MISO, J1.pin1, U1.MIDI_IN
  N11: J1.pin2, U1.NC1
  N12: J1.pin3, R1.Pin_0
  N13: J2.pin1, OLED1.GND
  N14: J2.pin3, OLED1.SCK
  N15: J2.pin4, OLED1.SDA
  N16: U1.MIDI_OUT, R1.Pin_1
